// Digital circuit 4bit_ALU.dlogic.dig as structural Verilog
module _4bit_ALU_dlogic (
  input  [2:0] SP,
  input  [3:0] A,
  input  [3:0] B,
  output [3:0] O,
  output Z,
  output Cout
);

  wire [0:0] _4bit_subtractor_1_p4_2;
  wire [2:0] _4bit_subtractor_1_p4;
  wire [3:0] and_1_out, or_1_out, xor_1_out;

  // _4bit_subtractor _4bit_subtractor_1: pin names not known; wires that end beside it: B, A, SP[0], {_4bit_subtractor_1_p4_2[0], _4bit_subtractor_1_p4}, Cout
  assign and_1_out = A & B;  // And and_1, 4 bits wide
  assign or_1_out = A | B;  // Or or_1, 4 bits wide
  assign xor_1_out = A ^ B;  // XOr xor_1, 4 bits wide
  Multiplexer #(.Selector_Bits(3), .Bits(4)) multiplexer_1 (
    .sel(SP), .in_0({_4bit_subtractor_1_p4_2[0], _4bit_subtractor_1_p4}),
    .in_1({_4bit_subtractor_1_p4_2[0], _4bit_subtractor_1_p4}), .in_2(and_1_out), .in_3(or_1_out),
    .in_4(xor_1_out), .in_5({3'b000, _4bit_subtractor_1_p4_2[0]}), .in_6(A), .in_7(B), .out(O));
  nor nor_1 (Z, _4bit_subtractor_1_p4[0], _4bit_subtractor_1_p4[1], _4bit_subtractor_1_p4[2], _4bit_subtractor_1_p4_2[0]);

  // Notes on the sheet:
  //   O: Could be literally 4 indivisual bits tho
endmodule
