// Digital circuit 4bit_Processor.dlogic.dig as structural Verilog
module _4bit_Processor_dlogic (
  input  CK,
  input  [3:0] D,
  input  [3:0] Address,
  input  L,
  input  [3:0] C1,
  input  [3:0] Clear,
  input  I,
  output ZF,
  output Cout,
  output [3:0] Testing_PC,
  output [3:0] Testing_RAM,
  output [3:0] Testing_IR,
  output [3:0] Testing_B,
  output [3:0] Testing_A,
  output [3:0] Testing_ALU,
  output [2:0] SP_ALU
);

  wire and_1_out, and_2_out, Decoder_add, Decoder_il, Decoder_rr1, Decoder_rr2, Decoder_we, Decoder_wr,
       not_1_out, not_2_out, not_3_out, or_1_out, or_2_out, or_3_out, State_Machine_d, State_Machine_e;
  wire [0:0] Decoder_sub, nor_1_out, State_Machine_f;
  wire [1:1] Decoder_and, Decoder_or;
  wire [2:0] multiplexer_3_out, multiplexer_5_out, or_4_out;
  wire [2:2] Decoder_slt, Decoder_xor;
  wire [3:0] multiplexer_1_out, multiplexer_2_out;

  and and_1 (and_1_out, Decoder_il, and_2_out);
  or or_1 (or_1_out, and_1_out, State_Machine_d);
  Program_Counter Program_Counter (.CK(CK), .I(or_1_out), .L(L), .D(Address), .O(Testing_PC));
  and and_2 (and_2_out, State_Machine_e, not_1_out);
  not not_1 (not_1_out, I);
  RAM__1 RAM_Block (.D(D), .SP(2'b01), .A(Testing_PC), .CK(CK), .C(Clear), .O(Testing_RAM));
  F_State_Machine__1 State_Machine (.I(I), .CK(CK), .F(State_Machine_f[0]), .D(State_Machine_d), .E(State_Machine_e));
  IR Instruction_Register (.SP({1'b0, State_Machine_f[0]}), .D(Testing_RAM), .CK(CK), .C(C1), .O(Testing_IR));
  Multiplexer #(.Bits(4)) multiplexer_1 (.sel(or_2_out), .in_0(4'b0000), .in_1(Testing_IR), .out(multiplexer_1_out));
  or or_2 (or_2_out, State_Machine_e, State_Machine_d);
  Multiplexer #(.Bits(4)) multiplexer_2 (
    .sel(Decoder_il), .in_0(Testing_ALU), .in_1(Testing_RAM), .out(multiplexer_2_out));
  F_opcode_Decoder Decoder (
    .A(multiplexer_1_out[3]), .B(multiplexer_1_out[2]), .C(multiplexer_1_out[1]), .D(multiplexer_1_out[0]),
    .RR1(Decoder_rr1), .RR2(Decoder_rr2), .WE(Decoder_we), .ADD(Decoder_add), .IL(Decoder_il),
    .WR(Decoder_wr), .SUB(Decoder_sub[0]), .OR(Decoder_or[1]), .AND(Decoder_and[1]), .XOR(Decoder_xor[2]),
    .SLT(Decoder_slt[2]));  // open: Test
  nor nor_1 (nor_1_out[0], Decoder_add, Decoder_sub[0], Decoder_and[1], Decoder_or[1], Decoder_xor[2], Decoder_slt[2]);
  FRegisterFile Register_File (
    .RR1(Decoder_rr1), .RR2(Decoder_rr2), .WR(Decoder_wr), .WD(multiplexer_2_out), .WE(Decoder_we), .CK(CK),
    .RD2(Testing_B), .RD1(Testing_A));
  or or_3 (or_3_out, Decoder_add, Decoder_sub[0], Decoder_and[1], Decoder_or[1], Decoder_xor[2], Decoder_slt[2]);
  not not_2 (not_2_out, Decoder_rr1);
  not not_3 (not_3_out, or_3_out);
  assign or_4_out = {2'b00, nor_1_out[0]} | {2'b00, Decoder_sub[0]} | {1'b0, Decoder_and[1], 1'b0} | {1'b0, {2{Decoder_or[1]}}} | {Decoder_xor[2], 2'b00} | {Decoder_slt[2], 1'b0, Decoder_slt[2]};  // Or or_4, 3 bits wide
  Multiplexer #(.Bits(3)) multiplexer_3 (.sel(not_2_out), .in_0(3'b111), .in_1(3'b110), .out(multiplexer_3_out));
  Multiplexer #(.Bits(3)) multiplexer_4 (.sel(not_3_out), .in_0(or_4_out), .in_1(multiplexer_3_out), .out(SP_ALU));
  Multiplexer #(.Bits(3)) multiplexer_5 (
    .sel(State_Machine_e), .in_0(multiplexer_3_out), .in_1(SP_ALU), .out(multiplexer_5_out));
  _4bit_ALU_dlogic ALU (.SP(multiplexer_5_out), .A(Testing_A), .B(Testing_B), .O(Testing_ALU), .Z(ZF), .Cout(Cout));

  // Notes on the sheet:
  //   Logic for Incrementing Twice
  //    for Immediate Load
  //   .
  //   Logic for Incrementing Once
  //   Logic for NOP:
  //   6 for the ALU represents A 
  //   7 for the ALU represents B
  //   Dictates when the Execute cycle starts
endmodule
