// Digital circuit FRegisterFile.dig as structural Verilog
module FRegisterFile (
  input  RR1,
  input  RR2,
  input  WR,
  input  [3:0] WD,
  input  WE,
  input  CK,
  output [3:0] RD2,
  output [3:0] RD1
);

  wire and_1_out, and_2_out, decoder_1_out_0, decoder_1_out_1, nor_1_out, not_1_out;
  wire [3:0] register_2_q, register_7_q;

  Decoder decoder_1 (.sel(WR), .out_0(decoder_1_out_0), .out_1(decoder_1_out_1));
  and and_1 (and_1_out, WE, decoder_1_out_0);
  and and_2 (and_2_out, WE, decoder_1_out_1);
  Register register_1 (.D(WD[3]), .C(CK), .en(and_1_out), .Q(register_7_q[3]));
  Register register_2 (.D(WD[3]), .C(CK), .en(and_2_out), .Q(register_2_q[3]));
  Register register_3 (.D(WD[2]), .C(CK), .en(and_1_out), .Q(register_7_q[2]));
  Register register_4 (.D(WD[2]), .C(CK), .en(and_2_out), .Q(register_2_q[2]));
  Register register_5 (.D(WD[1]), .C(CK), .en(and_1_out), .Q(register_7_q[1]));
  Register register_6 (.D(WD[1]), .C(CK), .en(and_2_out), .Q(register_2_q[1]));
  Register register_7 (.D(WD[0]), .C(CK), .en(and_1_out), .Q(register_7_q[0]));
  Register register_8 (.D(WD[0]), .C(CK), .en(and_2_out), .Q(register_2_q[0]));
  Multiplexer #(.Bits(4)) multiplexer_1 (.sel(nor_1_out), .in_0(register_2_q), .in_1(4'b0000), .out(RD2));
  not not_1 (not_1_out, RR2);
  Multiplexer #(.Bits(4)) multiplexer_2 (.sel(RR1), .in_0(register_7_q), .in_1(register_7_q), .out(RD1));
  nor nor_1 (nor_1_out, RR2, not_1_out);

  // Notes on the sheet:
  //   WE-WR Logic
  //   Register A
  //   Register B
  //   4bit data->1bit*5
  //   4bit data->1bit*4
  //   1bit*4->4bit
  //   RR1-RR2 Logic
endmodule
