// Digital circuit F_State_Machine (1).dig as structural Verilog
module F_State_Machine__1 (
  input  I,
  input  CK,
  output F,
  output D,
  output E
);

  wire and_1_out, and_2_out, and_3_out, and_4_out, and_5_out, not_1_out, not_2_out, not_3_out, not_4_out,
       or_1_out, or_2_out;
  wire [1:0] MSB_q;

  not not_1 (not_1_out, I);
  not not_2 (not_2_out, I);
  not not_3 (not_3_out, MSB_q[1]);
  not not_4 (not_4_out, MSB_q[0]);
  and and_1 (and_1_out, MSB_q[1], not_1_out);
  and and_2 (and_2_out, MSB_q[0], not_2_out);
  and and_3 (and_3_out, not_3_out, not_4_out);
  and and_4 (and_4_out, MSB_q[0], I);
  and and_5 (and_5_out, and_3_out, I);
  or or_1 (or_1_out, and_1_out, and_4_out);
  or or_2 (or_2_out, and_2_out, and_5_out);
  D_FF MSB (.D(or_1_out), .C(CK), .Q(MSB_q[1]));  // open: nQ
  D_FF LSB (.D(or_2_out), .C(CK), .Q(MSB_q[0]));  // open: nQ
  Decoder #(.Selector_Bits(2)) decoder_1 (.sel(MSB_q), .out_0(F), .out_1(D), .out_2(E));  // open: out_3

  // Notes on the sheet:
  //   DMSB Logic
  //   DLSB Logic
endmodule
