// Digital circuit F_opcode_Decoder.dig as structural Verilog
module F_opcode_Decoder (
  input  A,
  input  B,
  input  C,
  input  D,
  output RR1,
  output RR2,
  output WE,
  output ADD,
  output IL,
  output WR,
  output SUB,
  output OR,
  output AND,
  output XOR,
  output SLT,
  output Test
);

  wire and_1_out, and_2_out, and_3_out, and_4_out, and_5_out, and_6_out, not_1_out, not_2_out, not_3_out,
       not_4_out, not_5_out, not_6_out, not_7_out, not_8_out, not_9_out, not_10_out, not_11_out, not_12_out,
       not_13_out, not_14_out, not_15_out, not_16_out, not_17_out, not_18_out, not_19_out, not_20_out,
       not_21_out, not_22_out, not_23_out, not_24_out, not_25_out, not_26_out;

  not not_1 (not_1_out, A);
  not not_2 (not_2_out, B);
  not not_3 (not_3_out, D);
  not not_4 (not_4_out, A);
  not not_5 (not_5_out, B);
  not not_6 (not_6_out, C);
  and and_1 (and_1_out, not_1_out, not_2_out, C, not_3_out);
  and and_2 (and_2_out, not_4_out, not_5_out, not_6_out, D);
  or or_1 (Test, and_1_out, and_2_out);
  not not_7 (not_7_out, A);
  not not_8 (not_8_out, B);
  not not_9 (not_9_out, D);
  not not_10 (not_10_out, A);
  not not_11 (not_11_out, B);
  not not_12 (not_12_out, C);
  not not_13 (not_13_out, D);
  not not_14 (not_14_out, B);
  not not_15 (not_15_out, C);
  and and_3 (and_3_out, not_7_out, not_8_out, C, not_9_out);
  and and_4 (and_4_out, not_10_out, not_11_out, not_12_out, D);
  not not_16 (not_16_out, B);
  not not_17 (not_17_out, C);
  not not_18 (not_18_out, B);
  not not_19 (not_19_out, C);
  not not_20 (not_20_out, D);
  not not_21 (not_21_out, D);
  not not_22 (not_22_out, B);
  not not_23 (not_23_out, A);
  not not_24 (not_24_out, B);
  not not_25 (not_25_out, C);
  not not_26 (not_26_out, D);
  or or_2 (IL, and_3_out, and_4_out);
  and and_5 (and_5_out, not_22_out, not_23_out, C);
  and and_6 (and_6_out, not_24_out, not_25_out, not_26_out);
  and and_7 (ADD, A, not_16_out, not_17_out, D);
  and and_8 (SUB, A, not_14_out, C, not_20_out);
  and and_9 (AND, A, not_18_out, C, D);
  and and_10 (OR, A, B, not_15_out, not_13_out);
  and and_11 (XOR, A, B, not_19_out, D);
  and and_12 (SLT, A, B, C, not_21_out);
  or or_3 (WR, and_5_out, and_6_out);
  or or_4 (WE, C, D, A);
  not not_27 (RR1, A);

  assign RR2 = 1'b1;

  // Notes on the sheet:
  //   Opcode
  //   OR Logic
  //   ADD Logic
  //   SUB Logic
  //   AND Logic
  //   XOR Logic
  //   IL Logic
  //   SLT Logic
  //   WR Logic
  //   WE Logic
  //   Instructions
endmodule
