// Digital circuit IR.dig as structural Verilog
module IR (
  input  [1:0] SP,
  input  [3:0] D,
  input  CK,
  input  [3:0] C,
  output [3:0] O
);

  Register register_1 (.CK(CK), .SP(SP), .D(D), .C(C), .O(O));
endmodule
