// Digital circuit Program Counter.dig as structural Verilog
module Program_Counter (
  input  CK,
  input  I,
  input  L,
  input  [3:0] D,
  output [3:0] O
);

  wire and_1_out, not_1_out;
  wire [3:0] _4bit_full_adder_1_p2, multiplexer_1_out;

  not not_1 (not_1_out, I);
  and and_1 (and_1_out, not_1_out, L);
  Multiplexer #(.Bits(4)) multiplexer_1 (.sel(and_1_out), .in_0(O), .in_1(D), .out(multiplexer_1_out));
  // _4bit_full_adder _4bit_full_adder_1: pin names not known; wires that end beside it: {3'b000, I}, _4bit_full_adder_1_p2, 1'b0, O
  D_FF d_ff_1 (.D(multiplexer_1_out[3]), .C(CK), .Q(_4bit_full_adder_1_p2[3]));  // open: nQ
  D_FF d_ff_2 (.D(multiplexer_1_out[2]), .C(CK), .Q(_4bit_full_adder_1_p2[2]));  // open: nQ
  D_FF d_ff_3 (.D(multiplexer_1_out[1]), .C(CK), .Q(_4bit_full_adder_1_p2[1]));  // open: nQ
  D_FF d_ff_4 (.D(multiplexer_1_out[0]), .C(CK), .Q(_4bit_full_adder_1_p2[0]));  // open: nQ
endmodule
